# Fritzing sketch board (saved by Fritzing 1.0.1rc)
breadboards: 1

parts:
  S1 = Pushbutton [package="[THT]"]
  LED1 = LED - 5mm [color="Blue (430nm)" current=0.030A package="5 mm [THT]"]
  S2 = Pushbutton [package="[THT]"]
  R2 = Resistor [tolerance=±5% resistance=220 power=0.25W package=THT]
  LED2 = LED - 5mm [color="Red (635nm)" current=0.030A package="5 mm [THT]"]
  LED3 = LED - 5mm [color="Green (555nm)" current=0.030A package="5 mm [THT]"]
  S3 = Pushbutton [package="[THT]"]
  Part1 = Arduino Uno (Rev3)
  S4 = Pushbutton [package="[THT]"]
  LED4 = LED - 5mm [color="Yellow (585nm)" current=0.030A package="5 mm [THT]"]
  R3 = Resistor [tolerance=±5% resistance=220 power=0.25W package=THT]
  R4 = Resistor [tolerance=±5% resistance=220 power=0.25W package=THT]
  R5 = Resistor [tolerance=±5% resistance=220 power=0.25W package=THT]
  buz1 = Piezo Buzzer
  R6 = Resistor [tolerance=±5% resistance=220 power=0.25W package=THT]
  LED5 = 2-digit 7-segment [package=THT-longpads]
  IC1 = IC, DIP package, 16 pins [chip_label=IC]
  R7 = Resistor [tolerance=±5% resistance=220 power=0.25W package=THT]
  R8 = Resistor [tolerance=±5% resistance=220 power=0.25W package=THT]

nets:
  N1: S1.Pin_1, S1.Pin_2, S2.Pin_1, S2.Pin_2, S3.Pin_1, S3.Pin_2, Part1.GND, S4.Pin_1, S4.Pin_2, buz1.pin_1, IC1.pin8
  N2: S1.Pin_3, S1.Pin_4, LED1.cathode, Part1.D2
  N3: LED1.anode, R3.Pin_0
  N4: S2.Pin_3, S2.Pin_4, LED3.cathode, Part1.D3_PWM
  N5: R2.Pin_0, LED3.anode
  N6: R2.Pin_1, Part1.5V, R3.Pin_1, R4.Pin_1, R5.Pin_1, IC1.pin3, IC1.pin16
  N7: LED2.cathode, S3.Pin_3, S3.Pin_4, Part1.D4
  N8: LED2.anode, R4.Pin_0
  N9: Part1.D8, IC1.pin6
  N10: Part1.D9_PWM, IC1.pin2
  N11: Part1.D10_PWM/SS, IC1.pin1
  N12: Part1.D11_PWM/MOSI, R7.Pin_1
  N13: Part1.D12/MISO, R8.Pin_1
  N14: Part1.D5_PWM, S4.Pin_3, S4.Pin_4, LED4.cathode
  N15: Part1.D6_PWM, R6.Pin_1
  N16: Part1.D7, IC1.pin7
  N17: LED4.anode, R5.Pin_0
  N18: buz1.pin_2, R6.Pin_0
  N19: LED5.A, IC1.pin13
  N20: LED5.C, IC1.pin11
  N21: LED5.E, IC1.pin9
  N22: LED5.D, IC1.pin10
  N23: LED5.G, IC1.pin14
  N24: LED5.F, IC1.pin15
  N25: LED5.DIG2, R8.Pin_0
  N26: LED5.DIG1, R7.Pin_0
  N27: LED5.B, IC1.pin12

custom parts:
  Piezo Buzzer: Part from https://www.nutsvolts.com/magazine/article/november2012_SmileysWorkshop. Breadboard and icon images modified to be 0.3" in spacing and be more similar to the actual physical part.
  2-digit 7-segment: Most common two-digit seven-segment led indicator you can find on the internet. 10 legs: 2 common electrodes (one per each digit), 8 electrodes of each segment.
